# Fritzing sketch BigRedButton (saved by Fritzing 0.8.7b)

parts:
  Part2 = WiFly Module Breakout - Roving Networks (RN-131C)
  S1 = Round Pushbutton
  Part3 = USB LiPoly Charger
  ANT1 = Antenna  # not connected
  R1 = Resistor [tolerance=±5% resistance=10k package=THT]
  LED1 = LED - 5mm [color="Red (633nm)" package="5 mm [THT]"]
  R2 = Resistor [tolerance=±5% resistance=330 package=THT]
  Part1 = Arduino Pro Mini v13

nets:
  VCC: Part2.VCC, Part1.VCC
  GND: Part2.GND, Part3.GND, Part1.GND
  N1: Part2.UARTTX, Part1.D7
  N2: Part2.UARTRX, Part1.D8
  N3: S1.leg0, R1.Pin_0
  N4: Part3.VBAT, Part1.RAW
  N5: LED1.cathode, R2.Pin_0

notes:
  WiFly RN-131C

custom parts:
  WiFly Module Breakout - Roving Networks (RN-131C): Description: This is a simple breakout for the Roving Networks Bluetooth module. All pertinent pins are broken out and labeled. This new version's headers are unpopulated. Check below for appropriate headers. The module from Roving Networks is powerful, small, and very easy to use. This Bluetooth module is designed to replace serial cables. The Bluetooth stack is completely encapsulated. The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
